// Logisim project 7seg and comp.circ as structural Verilog
module _4_bit_com_main (
  input  A3,
  input  A2,
  input  A1,
  input  A0,
  input  B3,
  input  B2,
  input  B1,
  input  B0,
  output A_B,
  output A_B_2,
  output A_B_3
);

  _4_bit_comparator u_4_bit_comparator_1 (
    .A0(A0), .B0(B0), .A1(A1), .B1(B1), .A2(A2), .B2(B2), .A3(A3), .B3(B3), .A_B(A_B), .A_B_2(A_B_2),
    .A_B_3(A_B_3));

  // Notes on the sheet:
  //   2107103 & 2107104
  //   A=B
endmodule

module _1_bit_comparator (
  input  A,
  input  B,
  output A_B,
  output A_B_2,
  output A_B_3
);

  wire not_1_out, not_2_out;

  not not_1 (not_1_out, A);
  not not_2 (not_2_out, B);
  and and_1 (A_B, not_1_out, B);
  and and_2 (A_B_3, not_2_out, A);
  xnor xnor_1 (A_B_2, A_B, A_B_3);

  // Notes on the sheet:
  //   Roll : 2107104(Shakhoyat Rahman)
endmodule

module _2_bit_comparator (
  input  A0,
  input  B0,
  input  A1,
  input  B1,
  output A_B,
  output A_B_2,
  output A_B_3
);

  wire and_1_out, and_2_out, n1_bit_comparator_1_a_b, n1_bit_comparator_1_a_b_2, n1_bit_comparator_1_a_b_3,
       n1_bit_comparator_2_a_b, n1_bit_comparator_2_a_b_2, n1_bit_comparator_2_a_b_3;

  _1_bit_comparator u_1_bit_comparator_1 (
    .A(A0), .B(B0), .A_B(n1_bit_comparator_1_a_b), .A_B_2(n1_bit_comparator_1_a_b_2),
    .A_B_3(n1_bit_comparator_1_a_b_3));
  _1_bit_comparator u_1_bit_comparator_2 (
    .A(A1), .B(B1), .A_B(n1_bit_comparator_2_a_b), .A_B_2(n1_bit_comparator_2_a_b_2),
    .A_B_3(n1_bit_comparator_2_a_b_3));
  and and_1 (and_1_out, n1_bit_comparator_1_a_b, n1_bit_comparator_2_a_b_2);
  and and_2 (and_2_out, n1_bit_comparator_2_a_b_2, n1_bit_comparator_1_a_b_3);
  and and_3 (A_B_2, n1_bit_comparator_1_a_b_2, n1_bit_comparator_2_a_b_2);
  or or_1 (A_B_3, and_2_out, n1_bit_comparator_2_a_b_3);
  or or_2 (A_B, n1_bit_comparator_2_a_b, and_1_out);

  // Notes on the sheet:
  //   Roll: 2107104(Shakhoyat Rahman)
endmodule

module _4_bit_comparator (
  input  A0,
  input  B0,
  input  A1,
  input  B1,
  input  A2,
  input  B2,
  input  A3,
  input  B3,
  output A_B,
  output A_B_2,
  output A_B_3
);

  wire and_1_out, and_2_out, n2_bit_comparator_1_a_b, n2_bit_comparator_1_a_b_2, n2_bit_comparator_1_a_b_3,
       n2_bit_comparator_2_a_b, n2_bit_comparator_2_a_b_2, n2_bit_comparator_2_a_b_3;

  _2_bit_comparator u_2_bit_comparator_1 (
    .A0(A0), .B0(B0), .A1(A1), .B1(B1), .A_B(n2_bit_comparator_1_a_b), .A_B_2(n2_bit_comparator_1_a_b_2),
    .A_B_3(n2_bit_comparator_1_a_b_3));
  _2_bit_comparator u_2_bit_comparator_2 (
    .A0(A2), .B0(B2), .A1(A3), .B1(B3), .A_B(n2_bit_comparator_2_a_b), .A_B_2(n2_bit_comparator_2_a_b_2),
    .A_B_3(n2_bit_comparator_2_a_b_3));
  and and_1 (and_1_out, n2_bit_comparator_1_a_b, n2_bit_comparator_2_a_b_2);
  and and_2 (and_2_out, n2_bit_comparator_2_a_b_2, n2_bit_comparator_1_a_b_3);
  and and_3 (A_B_2, n2_bit_comparator_1_a_b_2, n2_bit_comparator_2_a_b_2);
  or or_1 (A_B, n2_bit_comparator_2_a_b, and_1_out);
  or or_2 (A_B_3, and_2_out, n2_bit_comparator_2_a_b_3);

  // Notes on the sheet:
  //   Roll:2107104(Shakhoyat Rahman)
endmodule

module _7_seg_main (
  input  A,
  input  B,
  input  C,
  input  D,
  output a_2,
  output b_2,
  output c_2,
  output d_2,
  output e,
  output f,
  output g
);

  a a_1 (.A(A), .B(B), .C(C), .D(D), .a_2(a_2));
  b b_1 (.A(A), .B(B), .C(C), .D(D), .b_2(b_2));
  c c_1 (.A(A), .B(B), .C(C), .D(D), .C_2(c_2));
  d d_1 (.A(A), .B(B), .C(C), .D(D), .d_2(d_2));
  e e_1 (.A(A), .B(B), .C(C), .D(D), .e(e));
  f f_1 (.A(A), .B(B), .C(C), .D(D), .f(f));
  g u_g (.A(A), .B(B), .C(C), .D(D), .g(g));

  // Notes on the sheet:
  //   A
  //   D
  //   C
  //   B
  //   Shakhoyat 2107104
endmodule

module a (
  input  A,
  input  B,
  input  C,
  input  D,
  output a_2
);

  wire and_1_out, and_2_out, and_3_out, and_4_out, and_5_out, and_6_out, not_1_out, not_2_out, not_3_out,
       not_4_out;

  not not_1 (not_1_out, B);
  not not_2 (not_2_out, A);
  not not_3 (not_3_out, C);
  not not_4 (not_4_out, D);
  and and_1 (and_1_out, not_1_out, not_4_out);
  and and_2 (and_2_out, not_2_out, C);
  and and_3 (and_3_out, not_2_out, B, D);
  and and_4 (and_4_out, B, C);
  and and_5 (and_5_out, A, not_1_out, not_3_out);
  and and_6 (and_6_out, A, not_4_out);
  or or_1 (a_2, and_1_out, and_2_out, and_3_out, and_4_out, and_5_out, and_6_out);

  // Notes on the sheet:
  //   A
  //   B
  //   D
  //   C
  //   a
endmodule

module b (
  input  A,
  input  B,
  input  C,
  input  D,
  output b_2
);

  wire and_1_out, and_2_out, and_3_out, and_4_out, and_5_out, not_1_out, not_2_out, not_3_out, not_4_out;

  not not_1 (not_1_out, B);
  not not_2 (not_2_out, A);
  not not_3 (not_3_out, C);
  not not_4 (not_4_out, D);
  and and_1 (and_1_out, not_1_out, not_2_out);
  and and_2 (and_2_out, not_1_out, not_4_out);
  and and_3 (and_3_out, not_2_out, not_3_out, not_4_out);
  and and_4 (and_4_out, not_2_out, C, D);
  and and_5 (and_5_out, A, not_3_out, D);
  or or_1 (b_2, and_1_out, and_2_out, and_3_out, and_4_out, and_5_out);

  // Notes on the sheet:
  //   A
  //   B
  //   D
  //   C
  //   b
endmodule

module c (
  input  A,
  input  B,
  input  C,
  input  D,
  output C_2
);

  wire and_1_out, and_2_out, and_3_out, and_4_out, and_5_out, not_1_out, not_2_out, not_3_out, not_4_out;

  not not_1 (not_1_out, B);
  not not_2 (not_2_out, A);
  not not_3 (not_3_out, C);
  not not_4 (not_4_out, D);
  and and_1 (and_1_out, not_2_out, not_3_out);
  and and_2 (and_2_out, not_2_out, D);
  and and_3 (and_3_out, not_3_out, D);
  and and_4 (and_4_out, not_2_out, B);
  and and_5 (and_5_out, A, not_1_out);
  or or_1 (C_2, and_1_out, and_2_out, and_3_out, and_4_out, and_5_out);

  // Notes on the sheet:
  //   A
  //   B
  //   C
  //   D
endmodule

module d (
  input  A,
  input  B,
  input  C,
  input  D,
  output d_2
);

  wire and_1_out, and_2_out, and_3_out, and_4_out, and_5_out, not_1_out, not_2_out, not_3_out, not_4_out;

  not not_1 (not_1_out, A);
  not not_2 (not_2_out, B);
  not not_3 (not_3_out, C);
  not not_4 (not_4_out, D);
  and and_1 (and_1_out, not_1_out, not_2_out, not_4_out);
  and and_2 (and_2_out, not_2_out, C, D);
  and and_3 (and_3_out, B, not_3_out, D);
  and and_4 (and_4_out, B, C, not_4_out);
  and and_5 (and_5_out, A, not_3_out);
  or or_1 (d_2, and_1_out, and_2_out, and_3_out, and_4_out, and_5_out);

  // Notes on the sheet:
  //   A
  //   B
  //   D
  //   C
endmodule

module e (
  input  A,
  input  B,
  input  C,
  input  D,
  output e
);

  wire and_1_out, and_2_out, and_3_out, and_4_out, not_1_out, not_2_out, not_3_out, not_4_out;

  not not_1 (not_1_out, A);
  not not_2 (not_2_out, B);
  not not_3 (not_3_out, C);
  not not_4 (not_4_out, D);
  and and_1 (and_1_out, not_2_out, not_4_out);
  and and_2 (and_2_out, C, not_4_out);
  and and_3 (and_3_out, A, C);
  and and_4 (and_4_out, A, B);
  or or_1 (e, and_1_out, and_2_out, and_3_out, and_4_out);

  // Notes on the sheet:
  //   A
  //   B
  //   C
  //   D
endmodule

module f (
  input  A,
  input  B,
  input  C,
  input  D,
  output f
);

  wire and_1_out, and_2_out, and_3_out, and_4_out, and_5_out, not_1_out, not_2_out, not_3_out, not_4_out;

  not not_1 (not_1_out, A);
  not not_2 (not_2_out, B);
  not not_3 (not_3_out, C);
  not not_4 (not_4_out, D);
  and and_1 (and_1_out, not_3_out, not_4_out);
  and and_2 (and_2_out, B, not_4_out);
  and and_3 (and_3_out, A, not_2_out);
  and and_4 (and_4_out, A, C);
  and and_5 (and_5_out, not_1_out, B, not_3_out);
  or or_1 (f, and_1_out, and_2_out, and_3_out, and_4_out, and_5_out);

  // Notes on the sheet:
  //   A
  //   B
  //   D
  //   C
endmodule

module g (
  input  A,
  input  B,
  input  C,
  input  D,
  output g
);

  wire and_1_out, and_2_out, and_3_out, and_4_out, and_5_out, not_1_out, not_2_out, not_3_out, not_4_out;

  not not_1 (not_1_out, A);
  not not_2 (not_2_out, B);
  not not_3 (not_3_out, C);
  not not_4 (not_4_out, D);
  and and_1 (and_1_out, not_2_out, C);
  and and_2 (and_2_out, C, not_4_out);
  and and_3 (and_3_out, A, not_2_out);
  and and_4 (and_4_out, A, D);
  and and_5 (and_5_out, not_1_out, B, not_3_out);
  or or_1 (g, and_1_out, and_2_out, and_3_out, and_4_out, and_5_out);

  // Notes on the sheet:
  //   A
  //   B
  //   D
  //   C
endmodule
