// Logisim project clock final.circ as structural Verilog: 5 circuits, main circuit main
module main (
);

  wire clock_1_out, hours_1__1a, hours_1__1b, hours_1__1c, hours_1__1d, hours_1__1e, hours_1__1f,
       hours_1__1g, hours_1__10a, hours_1__10b, hours_1__10c, hours_1__10d, hours_1__10e, hours_1__10f,
       hours_1__10g, minutes_1__1a, minutes_1__1b, minutes_1__1c, minutes_1__1d, minutes_1__1e,
       minutes_1__1f, minutes_1__1g, minutes_1__10a, minutes_1__10b, minutes_1__10c, minutes_1__10d,
       minutes_1__10e, minutes_1__10f, minutes_1__10g, minutes_1_clk_for_hour, seconds_1__1a, seconds_1__1b,
       seconds_1__1c, seconds_1__1d, seconds_1__1e, seconds_1__1f, seconds_1__1g, seconds_1__10a,
       seconds_1__10b, seconds_1__10c, seconds_1__10d, seconds_1__10e, seconds_1__10f, seconds_1__10g,
       seconds_1_clk_for_minute;

  _7_Segment_Display u_7_segment_display_1 (
    .g(hours_1__1g), .f(hours_1__1f), .a(hours_1__1a), .b(hours_1__1b), .e(hours_1__1e), .d(hours_1__1d),
    .c(hours_1__1c));  // open: dp
  _7_Segment_Display u_7_segment_display_2 (
    .g(hours_1__10g), .f(hours_1__10f), .a(hours_1__10a), .b(hours_1__10b), .e(hours_1__10e),
    .d(hours_1__10d), .c(hours_1__10c));  // open: dp
  Hours hours_1 (
    ._1a(hours_1__1a), ._1b(hours_1__1b), ._1c(hours_1__1c), ._1d(hours_1__1d), ._1e(hours_1__1e),
    ._1f(hours_1__1f), ._1g(hours_1__1g), .clk_from_minute(minutes_1_clk_for_hour), ._10a(hours_1__10a),
    ._10b(hours_1__10b), ._10c(hours_1__10c), ._10d(hours_1__10d), ._10e(hours_1__10e), ._10f(hours_1__10f),
    ._10g(hours_1__10g));
  _7_Segment_Display u_7_segment_display_3 (
    .g(minutes_1__1g), .f(minutes_1__1f), .a(minutes_1__1a), .b(minutes_1__1b), .e(minutes_1__1e),
    .d(minutes_1__1d), .c(minutes_1__1c));  // open: dp
  _7_Segment_Display u_7_segment_display_4 (
    .g(minutes_1__10g), .f(minutes_1__10f), .a(minutes_1__10a), .b(minutes_1__10b), .e(minutes_1__10e),
    .d(minutes_1__10d), .c(minutes_1__10c));  // open: dp
  Minutes minutes_1 (
    .clk_for_hour(minutes_1_clk_for_hour), ._1a(minutes_1__1a), ._1b(minutes_1__1b), ._1c(minutes_1__1c),
    ._1d(minutes_1__1d), ._1e(minutes_1__1e), ._1f(minutes_1__1f), ._1g(minutes_1__1g),
    .clk_from_second(seconds_1_clk_for_minute), ._10a(minutes_1__10a), ._10b(minutes_1__10b),
    ._10c(minutes_1__10c), ._10d(minutes_1__10d), ._10e(minutes_1__10e), ._10f(minutes_1__10f),
    ._10g(minutes_1__10g));
  _7_Segment_Display u_7_segment_display_5 (
    .g(seconds_1__1g), .f(seconds_1__1f), .a(seconds_1__1a), .b(seconds_1__1b), .e(seconds_1__1e),
    .d(seconds_1__1d), .c(seconds_1__1c));  // open: dp
  _7_Segment_Display u_7_segment_display_6 (
    .g(seconds_1__10g), .f(seconds_1__10f), .a(seconds_1__10a), .b(seconds_1__10b), .e(seconds_1__10e),
    .d(seconds_1__10d), .c(seconds_1__10c));  // open: dp
  Seconds seconds_1 (
    .clk_for_minute(seconds_1_clk_for_minute), ._1a(seconds_1__1a), ._1b(seconds_1__1b), ._1c(seconds_1__1c),
    ._1d(seconds_1__1d), ._1e(seconds_1__1e), ._1f(seconds_1__1f), ._1g(seconds_1__1g),
    .Clock_for_second(clock_1_out), ._10a(seconds_1__10a), ._10b(seconds_1__10b), ._10c(seconds_1__10c),
    ._10d(seconds_1__10d), ._10e(seconds_1__10e), ._10f(seconds_1__10f), ._10g(seconds_1__10g));
  Clock clock_1 (.out(clock_1_out));

  // Notes on the sheet:
  //   2107103
  //   Digital Clock
  //   by
  //   2107103 & 2107104
endmodule

module Hours (
  input  clk_from_minute,
  output _1a,
  output _10a,
  output _10b,
  output _1b,
  output _10c,
  output _1c,
  output _10d,
  output _1d,
  output _1e,
  output _10e,
  output _1f,
  output _10f,
  output _10g,
  output _1g
);

  wire and_1_out, and_2_out, main_1_a, main_1_b, main_1_c, main_2_a, main_2_b, main_2_c, main_2_d,
       n4_bit_com_main_1_a_b_2, n4_bit_com_main_2_a_b_2, not_1_out, not_2_out, not_3_out, not_4_out,
       not_5_out, not_6_out, not_7_out;

  not not_1 (not_1_out, 1'b1);
  not not_2 (not_2_out, 1'b1);
  mod6_main main_1 (.clk_input(and_1_out), .ifClr(and_2_out), .A(main_1_a), .B(main_1_b), .C(main_1_c));
  _4_bit_com_main u_4_bit_com_main_1 (
    .A3(not_1_out), .A2(main_1_a), .A1(main_1_b), .A0(main_1_c), .B3(not_2_out), .B2(not_2_out), .B1(1'b1),
    .B0(not_2_out), .A_B_2(n4_bit_com_main_1_a_b_2));  // open: A_B, A_B_3
  and and_1 (and_1_out, not_3_out, not_4_out, not_5_out, not_6_out);
  _7_seg_main u_7_seg_main_1 (
    .A(not_1_out), .B(main_1_a), .C(main_1_b), .D(main_1_c), .a_2(_10a), .b_2(_10b), .c_2(_10c), .d_2(_10d),
    .e(_10e), .f(_10f), .g(_10g));
  not not_3 (not_3_out, main_2_d);
  not not_4 (not_4_out, main_2_c);
  not not_5 (not_5_out, main_2_b);
  not not_6 (not_6_out, main_2_a);
  _7_seg_main u_7_seg_main_2 (
    .A(main_2_a), .B(main_2_b), .C(main_2_c), .D(main_2_d), .a_2(_1a), .b_2(_1b), .c_2(_1c), .d_2(_1d),
    .e(_1e), .f(_1f), .g(_1g));
  and and_2 (and_2_out, n4_bit_com_main_2_a_b_2, n4_bit_com_main_1_a_b_2);
  _4_bit_com_main u_4_bit_com_main_2 (
    .A3(main_2_a), .A2(main_2_b), .A1(main_2_c), .A0(main_2_d), .B3(not_7_out), .B2(1'b1), .B1(not_7_out),
    .B0(not_7_out), .A_B_2(n4_bit_com_main_2_a_b_2));  // open: A_B, A_B_3
  not not_7 (not_7_out, 1'b1);
  mod_10__1_main main_2 (
    .ifClr(and_2_out), .clk_input(clk_from_minute), .A(main_2_a), .B(main_2_b), .C(main_2_c), .D(main_2_d));

  // Notes on the sheet:
  //   2107103
endmodule

module Minutes (
  input  clk_from_second,
  output clk_for_hour,
  output _1a,
  output _10a,
  output _10b,
  output _1b,
  output _10c,
  output _1c,
  output _10d,
  output _1d,
  output _1e,
  output _10e,
  output _1f,
  output _10f,
  output _10g,
  output _1g
);

  wire and_2_out, and_3_out, and_4_out, and_5_out, and_6_out, and_7_out, and_8_out, and_9_out, and_10_out,
       and_11_out, and_12_out, main_1_a, main_1_b, main_1_c, main_2_a, main_2_b, main_2_c, main_2_d,
       n0_9up_counter_4_skip_1_a, n0_9up_counter_4_skip_1_b, n0_9up_counter_4_skip_1_c,
       n0_9up_counter_4_skip_1_d, n4_bit_com_main_1_a_b_2, not_1_out, not_2_out, not_3_out, not_4_out,
       not_5_out, not_6_out, not_7_out, not_8_out, not_9_out, not_10_out, not_11_out, not_12_out, not_13_out,
       not_14_out, not_15_out, not_16_out, not_17_out, not_18_out, not_19_out, or_1_out, or_2_out, or_3_out,
       or_4_out;

  and and_1 (clk_for_hour, 1'b1, not_3_out, not_4_out, not_5_out);
  not not_1 (not_1_out, 1'b1);
  not not_2 (not_2_out, 1'b1);
  not not_3 (not_3_out, main_1_c);
  not not_4 (not_4_out, main_1_b);
  not not_5 (not_5_out, main_1_a);
  mod6_main main_1 (.clk_input(and_2_out), .A(main_1_a), .B(main_1_b), .C(main_1_c));  // open: ifClr
  _4_bit_com_main u_4_bit_com_main_1 (
    .A3(not_1_out), .A2(main_1_a), .A1(main_1_b), .A0(main_1_c), .B3(not_2_out), .B2(1'b1), .B1(not_2_out),
    .B0(not_2_out), .A_B_2(n4_bit_com_main_1_a_b_2));  // open: A_B, A_B_3
  and and_2 (and_2_out, not_6_out, not_7_out, not_8_out, not_9_out);
  _7_seg_main u_7_seg_main_1 (
    .A(not_1_out), .B(main_1_a), .C(main_1_b), .D(main_1_c), .a_2(_10a), .b_2(_10b), .c_2(_10c), .d_2(_10d),
    .e(_10e), .f(_10f), .g(_10g));
  not not_6 (not_6_out, or_1_out);
  not not_7 (not_7_out, or_2_out);
  not not_8 (not_8_out, or_3_out);
  not not_9 (not_9_out, or_4_out);
  _7_seg_main u_7_seg_main_2 (
    .A(or_4_out), .B(or_3_out), .C(or_2_out), .D(or_1_out), .a_2(_1a), .b_2(_1b), .c_2(_1c), .d_2(_1d),
    .e(_1e), .f(_1f), .g(_1g));
  and and_3 (and_3_out, not_12_out, not_10_out, not_11_out, not_13_out, not_14_out);
  not not_10 (not_10_out, and_10_out);
  not not_11 (not_11_out, n4_bit_com_main_1_a_b_2);
  not not_12 (not_12_out, and_11_out);
  or or_1 (or_1_out, and_8_out, and_7_out);
  or or_2 (or_2_out, and_9_out, and_6_out);
  or or_3 (or_3_out, and_10_out, and_5_out);
  or or_4 (or_4_out, and_11_out, and_4_out);
  _0_9up_counter_4_skip u_0_9up_counter_4_skip_1 (
    .ifClr(and_3_out), .clk_input(clk_from_second), .A(n0_9up_counter_4_skip_1_a),
    .B(n0_9up_counter_4_skip_1_b), .C(n0_9up_counter_4_skip_1_c), .D(n0_9up_counter_4_skip_1_d));
  not not_13 (not_13_out, and_9_out);
  not not_14 (not_14_out, and_8_out);
  and and_4 (and_4_out, n0_9up_counter_4_skip_1_a, n4_bit_com_main_1_a_b_2);
  and and_5 (and_5_out, n0_9up_counter_4_skip_1_b, n4_bit_com_main_1_a_b_2);
  and and_6 (and_6_out, n0_9up_counter_4_skip_1_c, n4_bit_com_main_1_a_b_2);
  and and_7 (and_7_out, n0_9up_counter_4_skip_1_d, n4_bit_com_main_1_a_b_2);
  and and_8 (and_8_out, main_2_d, not_15_out);
  and and_9 (and_9_out, main_2_c, not_15_out);
  and and_10 (and_10_out, main_2_b, not_15_out);
  and and_11 (and_11_out, main_2_a, not_15_out);
  mod_10__1_main main_2 (
    .ifClr(and_12_out), .clk_input(clk_from_second), .A(main_2_a), .B(main_2_b), .C(main_2_c), .D(main_2_d));
  not not_15 (not_15_out, n4_bit_com_main_1_a_b_2);
  and and_12 (and_12_out, n4_bit_com_main_1_a_b_2, not_16_out, not_18_out, not_17_out, not_19_out);
  not not_16 (not_16_out, and_4_out);
  not not_17 (not_17_out, and_6_out);
  not not_18 (not_18_out, and_5_out);
  not not_19 (not_19_out, and_7_out);

  // Notes on the sheet:
  //   2107103
endmodule

module Seconds (
  input  Clock_for_second,
  output clk_for_minute,
  output _1a,
  output _10a,
  output _10b,
  output _1b,
  output _10c,
  output _1c,
  output _10d,
  output _1d,
  output _1e,
  output _10e,
  output _1f,
  output _10f,
  output _10g,
  output _1g
);

  wire and_2_out, and_3_out, and_4_out, and_5_out, and_6_out, and_7_out, and_8_out, and_9_out, and_10_out,
       and_11_out, and_12_out, main_1_a, main_1_b, main_1_c, main_2_a, main_2_b, main_2_c, main_2_d,
       n0_9up_counter_4_skip_1_a, n0_9up_counter_4_skip_1_b, n0_9up_counter_4_skip_1_c,
       n0_9up_counter_4_skip_1_d, n4_bit_com_main_1_a_b_2, not_1_out, not_2_out, not_3_out, not_4_out,
       not_5_out, not_6_out, not_7_out, not_8_out, not_9_out, not_10_out, not_11_out, not_12_out, not_13_out,
       not_14_out, not_15_out, not_16_out, not_17_out, not_18_out, not_19_out, or_1_out, or_2_out, or_3_out,
       or_4_out;

  and and_1 (clk_for_minute, 1'b1, not_3_out, not_4_out, not_5_out);
  not not_1 (not_1_out, 1'b1);
  not not_2 (not_2_out, 1'b1);
  not not_3 (not_3_out, main_1_c);
  not not_4 (not_4_out, main_1_b);
  not not_5 (not_5_out, main_1_a);
  mod6_main main_1 (.clk_input(and_2_out), .A(main_1_a), .B(main_1_b), .C(main_1_c));  // open: ifClr
  _4_bit_com_main u_4_bit_com_main_1 (
    .A3(not_1_out), .A2(main_1_a), .A1(main_1_b), .A0(main_1_c), .B3(not_2_out), .B2(1'b1), .B1(not_2_out),
    .B0(not_2_out), .A_B_2(n4_bit_com_main_1_a_b_2));  // open: A_B, A_B_3
  and and_2 (and_2_out, not_6_out, not_7_out, not_8_out, not_9_out);
  _7_seg_main u_7_seg_main_1 (
    .A(not_1_out), .B(main_1_a), .C(main_1_b), .D(main_1_c), .a_2(_10a), .b_2(_10b), .c_2(_10c), .d_2(_10d),
    .e(_10e), .f(_10f), .g(_10g));
  not not_6 (not_6_out, or_1_out);
  not not_7 (not_7_out, or_2_out);
  not not_8 (not_8_out, or_3_out);
  not not_9 (not_9_out, or_4_out);
  _7_seg_main u_7_seg_main_2 (
    .A(or_4_out), .B(or_3_out), .C(or_2_out), .D(or_1_out), .a_2(_1a), .b_2(_1b), .c_2(_1c), .d_2(_1d),
    .e(_1e), .f(_1f), .g(_1g));
  and and_3 (and_3_out, not_12_out, not_10_out, not_11_out, not_13_out, not_14_out);
  not not_10 (not_10_out, and_10_out);
  not not_11 (not_11_out, n4_bit_com_main_1_a_b_2);
  not not_12 (not_12_out, and_11_out);
  or or_1 (or_1_out, and_8_out, and_7_out);
  or or_2 (or_2_out, and_9_out, and_6_out);
  or or_3 (or_3_out, and_10_out, and_5_out);
  or or_4 (or_4_out, and_11_out, and_4_out);
  _0_9up_counter_4_skip u_0_9up_counter_4_skip_1 (
    .ifClr(and_3_out), .clk_input(Clock_for_second), .A(n0_9up_counter_4_skip_1_a),
    .B(n0_9up_counter_4_skip_1_b), .C(n0_9up_counter_4_skip_1_c), .D(n0_9up_counter_4_skip_1_d));
  not not_13 (not_13_out, and_9_out);
  not not_14 (not_14_out, and_8_out);
  and and_4 (and_4_out, n0_9up_counter_4_skip_1_a, n4_bit_com_main_1_a_b_2);
  and and_5 (and_5_out, n0_9up_counter_4_skip_1_b, n4_bit_com_main_1_a_b_2);
  and and_6 (and_6_out, n0_9up_counter_4_skip_1_c, n4_bit_com_main_1_a_b_2);
  and and_7 (and_7_out, n0_9up_counter_4_skip_1_d, n4_bit_com_main_1_a_b_2);
  and and_8 (and_8_out, main_2_d, not_15_out);
  and and_9 (and_9_out, main_2_c, not_15_out);
  and and_10 (and_10_out, main_2_b, not_15_out);
  and and_11 (and_11_out, main_2_a, not_15_out);
  mod_10__1_main main_2 (
    .ifClr(and_12_out), .clk_input(Clock_for_second), .A(main_2_a), .B(main_2_b), .C(main_2_c), .D(main_2_d));
  not not_15 (not_15_out, n4_bit_com_main_1_a_b_2);
  and and_12 (and_12_out, n4_bit_com_main_1_a_b_2, not_17_out, not_18_out, not_16_out, not_19_out);
  not not_16 (not_16_out, and_6_out);
  not not_17 (not_17_out, and_4_out);
  not not_18 (not_18_out, and_5_out);
  not not_19 (not_19_out, and_7_out);

  // Notes on the sheet:
  //   2107103
endmodule

// Mod10(4 skip)
module _0_9up_counter_4_skip (
  input  ifClr,
  input  clk_input,
  output A,
  output B,
  output C,
  output D
);

  wire and_1_out, and_2_out, and_3_out, and_4_out, or_1_out, or_2_out, TA_qn, TC_qn, TD_qn;

  and and_1 (and_1_out, A, D);
  and and_2 (and_2_out, D, B, C);
  or or_1 (or_1_out, and_1_out, and_2_out);
  and and_3 (and_3_out, D, C);
  and and_4 (and_4_out, TA_qn, D);
  or or_2 (or_2_out, TC_qn, B, TD_qn);
  T_Flip_Flop TA (.clk(clk_input), .T(or_1_out), .Q(A), .Qn(TA_qn), .reset(ifClr));  // open: preset, en
  T_Flip_Flop TB (.clk(clk_input), .T(and_3_out), .Q(B), .reset(ifClr));  // open: Qn, preset, en
  T_Flip_Flop TC (.clk(clk_input), .T(and_4_out), .Q(C), .Qn(TC_qn), .reset(ifClr));  // open: preset, en
  T_Flip_Flop TD (.clk(clk_input), .T(or_2_out), .Q(D), .Qn(TD_qn), .reset(ifClr));  // open: preset, en

  // Notes on the sheet:
  //   2107103
endmodule
