// Logisim project mod6.circ as structural Verilog: 1 circuit, main circuit main
module main (
  input  ifClr,
  input  clk_input,
  output A,
  output B,
  output C
);

  wire and_1_out, and_2_out, and_3_out, and_4_out, or_1_out, or_2_out, QA_qn, QB_qn, QC_qn;

  and and_1 (and_1_out, A, QC_qn);
  and and_2 (and_2_out, B, C);
  and and_3 (and_3_out, B, QC_qn);
  and and_4 (and_4_out, QA_qn, QB_qn, C);
  or or_1 (or_1_out, and_1_out, and_2_out);
  or or_2 (or_2_out, and_3_out, and_4_out);
  D_Flip_Flop QA (.clk(clk_input), .D(or_1_out), .Q(A), .Qn(QA_qn), .reset(ifClr));  // open: preset, en
  D_Flip_Flop QB (.clk(clk_input), .D(or_2_out), .Q(B), .Qn(QB_qn), .reset(ifClr));  // open: preset, en
  D_Flip_Flop QC (.clk(clk_input), .D(QC_qn), .Q(C), .Qn(QC_qn), .reset(ifClr));  // open: preset, en

  // Notes on the sheet:
  //   Roll:2107104
endmodule
