// Logisim project mod_10_-1.circ as structural Verilog: 1 circuit, main circuit main
module main (
  input  ifClr,
  input  clk_input,
  output A,
  output B,
  output C,
  output D
);

  wire and_1_out, and_2_out, and_3_out, and_4_out, and_5_out, and_6_out, and_7_out, or_1_out, or_2_out,
       or_3_out, QA_qn, QB_qn, QC_qn, QD_qn;

  and and_1 (and_1_out, A, QD_qn);
  and and_2 (and_2_out, D, C, B);
  and and_3 (and_3_out, B, QC_qn);
  and and_4 (and_4_out, B, QD_qn);
  and and_5 (and_5_out, QB_qn, C, D);
  and and_6 (and_6_out, C, QD_qn);
  and and_7 (and_7_out, QA_qn, QC_qn, D);
  or or_1 (or_1_out, and_1_out, and_2_out);
  or or_2 (or_2_out, and_6_out, and_7_out);
  or or_3 (or_3_out, and_3_out, and_4_out, and_5_out);
  D_Flip_Flop QA (.clk(clk_input), .D(or_1_out), .Q(A), .Qn(QA_qn), .reset(ifClr));  // open: preset, en
  D_Flip_Flop QB (.clk(clk_input), .D(or_3_out), .Q(B), .Qn(QB_qn), .reset(ifClr));  // open: preset, en
  D_Flip_Flop QC (.clk(clk_input), .D(or_2_out), .Q(C), .Qn(QC_qn), .reset(ifClr));  // open: preset, en
  D_Flip_Flop QD (.clk(clk_input), .D(QD_qn), .Q(D), .Qn(QD_qn), .reset(ifClr));  // open: preset, en

  // Notes on the sheet:
  //   ROLL:2107104
endmodule
